# Fritzing sketch SpaceInvaders-Arcade-scheme-STAGE2 (saved by Fritzing 0.9.3b)
breadboards: 1

parts:
  Bauteil1 = Arduino Uno (Rev3)  # not connected
  Bauteil2 = Arduino Motor Shield (Rev3)
  M2 = Stepper Motor - Bipolar
  M3 = Stepper Motor - Bipolar
  Bauteil3 = Thumb Joystick
  S1 = Pushbutton [package="[THT]"]
  S2 = Pushbutton [package="[THT]"]
  R1 = Resistor [tolerance=±5% resistance=220 package=THT]
  R2 = Resistor [tolerance=±5% resistance=220 package=THT]
  J1 = Basic Servo
  Grove1 = Grove OLED 128x96
  FLO-30_Circuit1 = FLO-30 Circuit
  FLO-30_Circuit2 = FLO-30 Circuit
  FLO-30_Circuit3 = FLO-30 Circuit
  FLO-30_Circuit4 = FLO-30 Circuit
  FLO-30_Circuit5 = FLO-30 Circuit
  FLO-30_Circuit6 = FLO-30 Circuit

nets:
  N1: Bauteil2.A0, Bauteil3.SEL
  N2: Bauteil2.A1, Bauteil3.HORZ
  N3: Bauteil2.A2, Bauteil3.VERT
  N4: Bauteil2.SDA, Grove1.SDA
  N5: Bauteil2.SCL, Grove1.SCL
  N6: Bauteil2.IOREF, FLO-30_Circuit1.RX
  N7: Bauteil2.D1/TX, FLO-30_Circuit6.TX
  N8: Bauteil2.D2, J1.pulse
  N9: Bauteil2.D4, S1.Pin_3, S1.Pin_4, R2.Pin_1
  N10: Bauteil2.D7, S2.Pin_3, S2.Pin_4, R1.Pin_1
  N11: Bauteil2.B-, M2.B
  N12: Bauteil2.B+, M2.A
  N13: Bauteil2.A-, M3.B
  N14: Bauteil2.A+, M3.A
  GND: Bauteil2.GND, M2.C, M2.D, M3.C, M3.D, Bauteil3.GND, R1.Pin_0, R2.Pin_0, J1.gnd, Grove1.GND, FLO-30_Circuit1.GND, FLO-30_Circuit2.GND, FLO-30_Circuit3.GND, FLO-30_Circuit4.GND, FLO-30_Circuit5.GND, FLO-30_Circuit6.GND
  VCC: Bauteil2.5V, Bauteil3.VCC, S1.Pin_1, S1.Pin_2, S2.Pin_1, S2.Pin_2, J1.vcc, Grove1.VCC, FLO-30_Circuit1.Vcc, FLO-30_Circuit2.Vcc, FLO-30_Circuit3.Vcc, FLO-30_Circuit4.Vcc, FLO-30_Circuit5.Vcc, FLO-30_Circuit6.Vcc
  N15: FLO-30_Circuit1.TX, FLO-30_Circuit2.RX
  N16: FLO-30_Circuit2.TX, FLO-30_Circuit4.RX
  N17: FLO-30_Circuit3.TX, FLO-30_Circuit5.RX
  N18: FLO-30_Circuit3.RX, FLO-30_Circuit4.TX
  N19: FLO-30_Circuit5.TX, FLO-30_Circuit6.RX
